// Logisim project s-mips.circ as structural Verilog: 12 circuits, main circuit RAM
module S_MIPS_Board (
  output halt
);

  wire button_1_out, CLK, CS, d_ff_1_q, R_W, Reset_out, RST, TTY_EN;
  wire [2:0] KDB;
  wire [3:0] Mask, ram_1_read_time, ram_1_write_time;
  wire [6:0] KDB_DATA, TTY_DATA;
  wire [15:0] Addr;
  wire [31:0] ram_1_data_out_0, ram_1_data_out_1, ram_1_data_out_2, ram_1_data_out_3, s_mips_1_ram_in_0,
       s_mips_1_ram_in_1, s_mips_1_ram_in_2, s_mips_1_ram_in_3;

  TTY #(.rows(25), .cols(80)) tty_1 (.data(TTY_DATA), .clk(CLK), .we(TTY_EN), .clr(RST));
  RAM ram_1 (
    .Address(Addr), .Data_Out_0(ram_1_data_out_0), .Data_Out_1(ram_1_data_out_1),
    .Data_Out_2(ram_1_data_out_2), .Data_Out_3(ram_1_data_out_3), .Data_In_0(s_mips_1_ram_in_0),
    .Data_In_1(s_mips_1_ram_in_1), .Data_In_2(s_mips_1_ram_in_2), .Data_In_3(s_mips_1_ram_in_3), .Mask(Mask),
    .nRead_Write(R_W), .Chip_Select(CS), .Read_Time(ram_1_read_time), .Reset(button_1_out),
    .Write_Time(ram_1_write_time));
  Button button_1 (.out(button_1_out));
  Keyboard #(.buflen(64)) keyboard_1 (.clk(CLK), .re(KDB[0]), .avail(KDB[2]), .data(KDB_DATA));  // open: clr
  S_MIPS s_mips_1 (
    .Kbd_Enable(KDB[0]), .Address(Addr), .Kbd_Clear(KDB[1]), .Kbd_Available(KDB[2]),
    .RAM_In_0(s_mips_1_ram_in_0), .Kbd_ASCII_Data(KDB_DATA), .RAM_In_1(s_mips_1_ram_in_1),
    .TTY_Enable(TTY_EN), .RAM_In_2(s_mips_1_ram_in_2), .RAM_In_3(s_mips_1_ram_in_3),
    .TTY_ASCII_Data(TTY_DATA), .Reset(RST), .RAM_Out_0(ram_1_data_out_0), .Clock(CLK),
    .RAM_Out_1(ram_1_data_out_1), .Stop(halt), .RAM_Out_2(ram_1_data_out_2), .RAM_Out_3(ram_1_data_out_3),
    .Mask(Mask), .Read_Time(ram_1_read_time), .Write_Time(ram_1_write_time), .nRead_Write(R_W),
    .Chip_Select(CS));
  D_Flip_Flop d_ff_1 (.clk(CLK), .D(1'b1), .Q(d_ff_1_q), .reset(Reset_out));  // open: Qn, preset, en
  Button Reset (.out(Reset_out));
  Clock clock_1 (.out(CLK));
  D_Flip_Flop d_ff_2 (.clk(CLK), .D(d_ff_1_q), .Qn(RST), .reset(Reset_out));  // open: Q, preset, en

  // Notes on the sheet:
  //   NO MODIFICAR
  //   Keyboard
endmodule

module RAM (
  input  [15:0] Address,
  input  [31:0] Data_In_0,
  input  [31:0] Data_In_1,
  input  [31:0] Data_In_2,
  input  [31:0] Data_In_3,
  input  [3:0] Mask,
  input  nRead_Write,
  input  Chip_Select,
  input  Reset,
  output [31:0] Data_Out_0,
  output [31:0] Data_Out_1,
  output [31:0] Data_Out_2,
  output [31:0] Data_Out_3,
  output [3:0] Read_Time,
  output [3:0] Write_Time
);

  wire and_2_out, and_3_out, and_4_out, and_5_out, and_6_out, and_7_out, and_8_out, and_9_out, Changed, CLK,
       comparator_2_eq, comparator_3_eq, comparator_4_eq, comparator_5_eq, comparator_6_eq, Count,
       demultiplexer_3_out0, Idle, Idle_q, Load, Load0, Load1, nand_1_out, or_1_out, or_2_out, or_3_out,
       or_4_out, or_5_out, or_6_out, or_7_out, or_8_out, or_9_out, or_10_out, Proc_q, Update_Mem, Zero_Time;
  wire [3:0] counter_1_q, multiplexer_1_out, subtractor_1_out;
  wire [31:0] register_1_q, register_2_q, register_3_q, register_4_q, register_5_q;

  // Probe on 4'b0011
  // Probe on 4'b0101
  Multiplexer #(.width(4), .enable("false")) multiplexer_1 (
    .in0(4'b0011), .in1(4'b0101), .out(multiplexer_1_out), .sel(nRead_Write));
  or or_1 (or_1_out, Idle, Update_Mem);
  or or_2 (or_2_out, ~Chip_Select, Reset);  // OR_Gate
  Subtractor #(.width(4)) subtractor_1 (.a(multiplexer_1_out), .b(4'b0010), .out(subtractor_1_out));  // open: bin, bout
  Demultiplexer #(.enable("false")) demultiplexer_1 (.out0(Idle), .out1(Load0), .in(Idle_q), .sel(Changed));
  D_Flip_Flop u_Idle (.clk(CLK), .D(or_1_out), .Q(Idle_q), .preset(or_2_out));  // open: Qn, en, reset
  // Probe on counter_1_q
  Counter #(.width(4), .max('hf)) counter_1 (
    .load(Load), .D(subtractor_1_out), .count(Count), .Q(counter_1_q), .clk(CLK), .clr(or_3_out));  // open: carry
  or or_3 (or_3_out, ~Chip_Select, Reset);  // OR_Gate
  Comparator #(.width(4), .mode("unsigned")) comparator_1 (
    .a(4'b0000), .b(counter_1_q), .eq(Zero_Time));  // open: gt, lt
  or or_4 (or_4_out, Count, Load0, Load1);
  Register #(.width(32)) register_1 (.D(Data_In_0), .en(Chip_Select), .Q(register_1_q), .clk(CLK), .clr(or_5_out));
  or or_5 (or_5_out, ~Chip_Select, Reset);  // OR_Gate
  Register #(.width(32)) register_2 (.D(Data_In_1), .en(Chip_Select), .Q(register_2_q), .clk(CLK), .clr(or_6_out));
  or or_6 (or_6_out, ~Chip_Select, Reset);  // OR_Gate
  Register #(.width(32)) register_3 (.D(Data_In_2), .en(Chip_Select), .Q(register_3_q), .clk(CLK), .clr(or_7_out));
  or or_7 (or_7_out, ~Chip_Select, Reset);  // OR_Gate
  Register #(.width(32)) register_4 (.D(Data_In_3), .en(Chip_Select), .Q(register_4_q), .clk(CLK), .clr(or_8_out));
  or or_8 (or_8_out, ~Chip_Select, Reset);  // OR_Gate
  Register #(.width(32)) register_5 (
    .D({{11{1'b1}}, nRead_Write, Mask, Address}), .en(Chip_Select), .Q(register_5_q), .clk(CLK),
    .clr(or_9_out));
  or or_9 (or_9_out, ~Chip_Select, Reset);  // OR_Gate
  D_Flip_Flop Proc (.clk(CLK), .D(or_4_out), .Q(Proc_q), .reset(or_10_out));  // open: Qn, preset, en
  or or_10 (or_10_out, ~Chip_Select, Reset);  // OR_Gate
  Demultiplexer #(.enable("false")) demultiplexer_2 (
    .out0(Count), .out1(Update_Mem), .in(demultiplexer_3_out0), .sel(Zero_Time));
  Demultiplexer #(.enable("false")) demultiplexer_3 (
    .out0(demultiplexer_3_out0), .out1(Load1), .in(Proc_q), .sel(Changed));
  Clock clock_1 (.out(CLK));
  Comparator #(.width(32)) comparator_2 (.a(register_1_q), .b(Data_In_0), .eq(comparator_2_eq));  // open: gt, lt
  Comparator #(.width(32)) comparator_3 (.a(register_2_q), .b(Data_In_1), .eq(comparator_3_eq));  // open: gt, lt
  Comparator #(.width(32)) comparator_4 (.a(register_3_q), .b(Data_In_2), .eq(comparator_4_eq));  // open: gt, lt
  Comparator #(.width(32)) comparator_5 (.a(register_4_q), .b(Data_In_3), .eq(comparator_5_eq));  // open: gt, lt
  Comparator #(.width(32)) comparator_6 (
    .a(register_5_q), .b({{11{1'b1}}, nRead_Write, Mask, Address}), .eq(comparator_6_eq));  // open: gt, lt
  nand nand_1 (nand_1_out, comparator_6_eq, comparator_2_eq, comparator_3_eq, comparator_4_eq, comparator_5_eq);
  and and_1 (Changed, nand_1_out, Chip_Select);
  or or_11 (Load, Count, Load1, Load0);
  and and_2 (and_2_out, Mask[0], Update_Mem, nRead_Write);
  and and_3 (and_3_out, Mask[1], Update_Mem, nRead_Write);
  and and_4 (and_4_out, Mask[2], Update_Mem, nRead_Write);
  and and_5 (and_5_out, Mask[3], Update_Mem, nRead_Write);
  RAM_part #(.addrWidth(16), .dataWidth(32), .bus("separate")) ram_1 (
    .addr(Address), .din(Data_In_0), .data(Data_Out_0), .str(and_2_out), .sel(Chip_Select), .clk(CLK),
    .ld(and_6_out), .clr(Reset));
  and and_6 (and_6_out, ~nRead_Write, Idle);  // AND_Gate
  RAM_part #(.addrWidth(16), .dataWidth(32), .bus("separate")) ram_2 (
    .addr(Address), .din(Data_In_1), .data(Data_Out_1), .str(and_3_out), .sel(Chip_Select), .clk(CLK),
    .ld(and_7_out), .clr(Reset));
  and and_7 (and_7_out, ~nRead_Write, Idle);  // AND_Gate
  RAM_part #(.addrWidth(16), .dataWidth(32), .bus("separate")) ram_3 (
    .addr(Address), .din(Data_In_2), .data(Data_Out_2), .str(and_4_out), .sel(Chip_Select), .clk(CLK),
    .ld(and_8_out), .clr(Reset));
  and and_8 (and_8_out, ~nRead_Write, Idle);  // AND_Gate
  RAM_part #(.addrWidth(16), .dataWidth(32), .bus("separate")) ram_4 (
    .addr(Address), .din(Data_In_3), .data(Data_Out_3), .str(and_5_out), .sel(Chip_Select), .clk(CLK),
    .ld(and_9_out), .clr(Reset));
  and and_9 (and_9_out, ~nRead_Write, Idle);  // AND_Gate

  assign Read_Time = 4'b0011;
  assign Write_Time = 4'b0101;

  // Other names for the same wires on the sheet: M0 = Mask[0]; M1 = Mask[1]; M2 = Mask[2]; M3 = Mask[3];
  //   RW = nRead_Write; CLR = Reset; CS = Chip_Select; Load2 = Count

  // Notes on the sheet:
  //   NO MODIFICAR
  //   excepto quizás los valores RT y WT
  //   BANK0
  //   BANK1
  //   BANK2
  //   BANK3
endmodule

module S_MIPS (
  input  Kbd_Available,
  input  [6:0] Kbd_ASCII_Data,
  input  [31:0] RAM_Out_0,
  input  [31:0] RAM_Out_1,
  input  Reset,
  input  [31:0] RAM_Out_2,
  input  Clock,
  input  [31:0] RAM_Out_3,
  input  [3:0] Read_Time,
  input  [3:0] Write_Time,
  output Kbd_Enable,
  output [15:0] Address,
  output Kbd_Clear,
  output TTY_Enable,
  output [6:0] TTY_ASCII_Data,
  output Stop,
  output [31:0] RAM_In_0,
  output [31:0] RAM_In_1,
  output [31:0] RAM_In_2,
  output [31:0] RAM_In_3,
  output [3:0] Mask,
  output nRead_Write,
  output Chip_Select
);

  wire control_unit_1_out_17, control_unit_1_out_18, control_unit_1_out_19, CS0, CS1, data_path_1_out_15,
       data_path_1_out_16, data_path_1_out_17, data_path_1_out_19, RW0, RW1;
  wire [1:0] control_unit_1_seladr, control_unit_1_selv, data_path_1_out_21, data_path_1_out_22;
  wire [2:0] data_path_1_out_23;
  wire [31:0] bit_extender_1_out, data_path_1_out_26, multiplexer_1_out, multiplexer_2_out;
  wire [31:7] data_path_1_tty;

  or or_1 (nRead_Write, RW0, RW1);
  or or_2 (Chip_Select, CS0, CS1);
  assign bit_extender_1_out = {{25{1'b0}}, Kbd_ASCII_Data};  // Bit_Extender bit_extender_1
  Multiplexer #(.width(32), .enable("false")) multiplexer_1 (
    .in0({32{1'b1}}), .in1(bit_extender_1_out), .out(multiplexer_1_out), .sel(Kbd_Available));
  Control_Unit control_unit_1 (
    .in_1(Reset), .in_2(Clock), .in_4(data_path_1_out_15), .in_3(data_path_1_out_16),
    .in_7(data_path_1_out_22), .in_8(Read_Time), .in_10(Write_Time), .SelAdr(control_unit_1_seladr),
    .SelV(control_unit_1_selv), .out_15(TTY_Enable), .out_17(control_unit_1_out_17),
    .out_18(control_unit_1_out_18), .out_20(RW0), .Ins_C(data_path_1_out_23), .in_5(data_path_1_out_17),
    .in_6(data_path_1_out_19), .out_13(CS0), .Halt(Stop), .out_19(control_unit_1_out_19), .out_16(Kbd_Enable));
  Data_Path data_path_1 (
    .in_1(Reset), .in_3(Clock), .in_5(control_unit_1_out_18), .in_6(control_unit_1_out_17),
    .in_7(control_unit_1_selv), .in_8(control_unit_1_seladr), .in_9(Read_Time), .in_10(RAM_Out_0),
    .in_11(RAM_Out_1), .in_12(RAM_Out_2), .in_13(RAM_Out_3), .in_14(multiplexer_1_out),
    .out_16(data_path_1_out_16), .out_17(data_path_1_out_17), .out_18(RW1), .out_19(data_path_1_out_19),
    .out_20(CS1), .out_21(data_path_1_out_21), .out_22(data_path_1_out_22), .out_23(data_path_1_out_23),
    .out_24(Mask), .out_25(Address), .out_26(data_path_1_out_26), .TTY({data_path_1_tty, TTY_ASCII_Data}),
    .out_15(data_path_1_out_15), .in_4(RW0), .in_2(control_unit_1_out_19));
  Multiplexer #(.width(32), .enable("false")) multiplexer_2 (
    .in0({32{1'b0}}), .in1(data_path_1_out_26), .out(multiplexer_2_out), .sel(nRead_Write));
  Demultiplexer #(.select(2), .width(32), .enable("false")) demultiplexer_1 (
    .out0(RAM_In_0), .out1(RAM_In_1), .out2(RAM_In_2), .out3(RAM_In_3),
    .in({multiplexer_2_out[7:0], multiplexer_2_out[15:8], multiplexer_2_out[23:16], multiplexer_2_out[31:24]}),
    .sel(data_path_1_out_21));
  // Probe on data_path_1_out_21

  assign Kbd_Clear = Reset;

  // Other names for the same wires on the sheet: TTY_DATA[6:0] = TTY_ASCII_Data; CLK = Clock; CS = Chip_Select;
  //   KBD_AVAIL = Kbd_Available; CLR = Reset; KBD_CLR = Reset; KBD_DATA[6:0] = Kbd_ASCII_Data; RAM_A[15:0] = Address;
  //   RAM_INPUT_0[31:0] = RAM_In_0; RAM_INPUT_1[31:0] = RAM_In_1; RAM_INPUT_2[31:0] = RAM_In_2;
  //   RAM_INPUT_3[31:0] = RAM_In_3; RAM_MASK[3:0] = Mask; RAM_OUTPUT_0[31:0] = RAM_Out_0;
  //   RAM_OUTPUT_1[31:0] = RAM_Out_1; RAM_OUTPUT_2[31:0] = RAM_Out_2; RAM_OUTPUT_3[31:0] = RAM_Out_3;
  //   RW = nRead_Write

  // Notes on the sheet:
  //   RAM ADDRESS
  //   DATA FROM RAM
  //   DATA TO RAM
  //   DATA WRITE MASK
  //   RAM TIMING
  //   RAM CONTROL
  //   KEYBOARD
  //   TTY
  //   SEQUENCING
endmodule

module Register_File (
  input  RW,
  input  [4:0] in_2,
  input  [4:0] Adress,
  input  in_4,
  input  in_5,
  input  [31:0] in_6,
  input  in_7,
  input  [31:0] in_8,
  input  [31:0] in_9,
  input  [4:0] in_10,
  input  in_11,
  output [31:0] Output_1,
  output [31:0] Output_2,
  output [31:0] Output_High___Low
);

  wire R1, R2, R3, R4, R5, R6, R7, R8, R9, R10, R11, R12, R13, R14, R15, R16, R17, R18, R19, R20, R21, R22,
       R23, R24, R25, R26, R27, R28, R29, R30, R31;
  wire [31:0] Hi, Lo, O0, O1, O2, O3, O4, O5, O6, O7, O8, O9, O10, O11, O12, O13, O14, O15, O16, O17, O18,
       O19, O20, O21, O22, O23, O24, O25, O26, O27, O28, O29, O30, O31;

  Demultiplexer #(.select(5), .enable("false")) demultiplexer_1 (
    .out1(R1), .out2(R2), .out3(R3), .out4(R4), .out5(R5), .out6(R6), .out7(R7), .out8(R8), .out9(R9),
    .out10(R10), .out11(R11), .out12(R12), .out13(R13), .out14(R14), .out15(R15), .out16(R16), .out17(R17),
    .out18(R18), .out19(R19), .out20(R20), .out21(R21), .out22(R22), .out23(R23), .out24(R24), .out25(R25),
    .out26(R26), .out27(R27), .out28(R28), .out29(R29), .out30(R30), .out31(R31), .in(RW), .sel(Adress));  // open: out0
  Register #(.width(32)) register_1 (.D(in_6), .en(1'b0), .Q(O0), .clk(in_4), .clr(in_5));
  Register #(.width(32)) register_2 (.D(in_6), .en(R8), .Q(O8), .clk(in_4), .clr(in_5));
  Register #(.width(32)) register_3 (.D(in_6), .en(R16), .Q(O16), .clk(in_4), .clr(in_5));
  Register #(.width(32)) register_4 (.D(in_6), .en(R24), .Q(O24), .clk(in_4), .clr(in_5));
  Register #(.width(32)) register_5 (.D(in_9), .en(in_11), .Q(Lo), .clk(in_4), .clr(in_5));
  Multiplexer #(.width(32), .enable("false")) multiplexer_1 (.in0(Hi), .in1(Lo), .out(Output_High___Low), .sel(in_7));
  Register #(.width(32)) register_6 (.D(in_6), .en(R1), .Q(O1), .clk(in_4), .clr(in_5));
  Register #(.width(32)) register_7 (.D(in_6), .en(R9), .Q(O9), .clk(in_4), .clr(in_5));
  Register #(.width(32)) register_8 (.D(in_6), .en(R17), .Q(O17), .clk(in_4), .clr(in_5));
  Register #(.width(32)) register_9 (.D(in_6), .en(R25), .Q(O25), .clk(in_4), .clr(in_5));
  Register #(.width(32)) register_10 (.D(in_8), .en(in_11), .Q(Hi), .clk(in_4), .clr(in_5));
  Register #(.width(32)) register_11 (.D(in_6), .en(R2), .Q(O2), .clk(in_4), .clr(in_5));
  Register #(.width(32)) register_12 (.D(in_6), .en(R10), .Q(O10), .clk(in_4), .clr(in_5));
  Register #(.width(32)) register_13 (.D(in_6), .en(R18), .Q(O18), .clk(in_4), .clr(in_5));
  Register #(.width(32)) register_14 (.D(in_6), .en(R26), .Q(O26), .clk(in_4), .clr(in_5));
  Register #(.width(32)) register_15 (.D(in_6), .en(R3), .Q(O3), .clk(in_4), .clr(in_5));
  Register #(.width(32)) register_16 (.D(in_6), .en(R11), .Q(O11), .clk(in_4), .clr(in_5));
  Register #(.width(32)) register_17 (.D(in_6), .en(R19), .Q(O19), .clk(in_4), .clr(in_5));
  Register #(.width(32)) register_18 (.D(in_6), .en(R27), .Q(O27), .clk(in_4), .clr(in_5));
  Register #(.width(32)) register_19 (.D(in_6), .en(R4), .Q(O4), .clk(in_4), .clr(in_5));
  Register #(.width(32)) register_20 (.D(in_6), .en(R12), .Q(O12), .clk(in_4), .clr(in_5));
  Register #(.width(32)) register_21 (.D(in_6), .en(R20), .Q(O20), .clk(in_4), .clr(in_5));
  Register #(.width(32)) register_22 (.D(in_6), .en(R28), .Q(O28), .clk(in_4), .clr(in_5));
  Register #(.width(32)) register_23 (.D(in_6), .en(R5), .Q(O5), .clk(in_4), .clr(in_5));
  Register #(.width(32)) register_24 (.D(in_6), .en(R13), .Q(O13), .clk(in_4), .clr(in_5));
  Register #(.width(32)) register_25 (.D(in_6), .en(R21), .Q(O21), .clk(in_4), .clr(in_5));
  Register #(.width(32)) register_26 (.D(in_6), .en(R29), .Q(O29), .clk(in_4), .clr(in_5));
  Register #(.width(32)) register_27 (.D(in_6), .en(R6), .Q(O6), .clk(in_4), .clr(in_5));
  Register #(.width(32)) register_28 (.D(in_6), .en(R14), .Q(O14), .clk(in_4), .clr(in_5));
  Register #(.width(32)) register_29 (.D(in_6), .en(R22), .Q(O22), .clk(in_4), .clr(in_5));
  Register #(.width(32)) register_30 (.D(in_6), .en(R30), .Q(O30), .clk(in_4), .clr(in_5));
  Register #(.width(32)) register_31 (.D(in_6), .en(R7), .Q(O7), .clk(in_4), .clr(in_5));
  Register #(.width(32)) register_32 (.D(in_6), .en(R15), .Q(O15), .clk(in_4), .clr(in_5));
  Register #(.width(32)) register_33 (.D(in_6), .en(R23), .Q(O23), .clk(in_4), .clr(in_5));
  Register #(.width(32)) register_34 (.D(in_6), .en(R31), .Q(O31), .clk(in_4), .clr(in_5));
  Multiplexer #(.select(5), .width(32), .enable("false")) multiplexer_2 (
    .in0(O0), .in1(O1), .in2(O2), .in3(O3), .in4(O4), .in5(O5), .in6(O6), .in7(O7), .in8(O8), .in9(O9),
    .in10(O10), .in11(O11), .in12(O12), .in13(O13), .in14(O14), .in15(O15), .in16(O16), .in17(O17),
    .in18(O18), .in19(O19), .in20(O20), .in21(O21), .in22(O22), .in23(O23), .in24(O24), .in25(O25),
    .in26(O26), .in27(O27), .in28(O30), .in29(O29), .in30(O30), .in31(O31), .out(Output_1), .sel(in_2));
  Multiplexer #(.select(5), .width(32), .enable("false")) multiplexer_3 (
    .in0(O0), .in1(O1), .in2(O2), .in3(O3), .in4(O4), .in5(O5), .in6(O6), .in7(O7), .in8(O8), .in9(O9),
    .in10(O10), .in11(O11), .in12(O12), .in13(O13), .in14(O14), .in15(O15), .in16(O16), .in17(O17),
    .in18(O18), .in19(O19), .in20(O20), .in21(O21), .in22(O22), .in23(O23), .in24(O24), .in25(O25),
    .in26(O26), .in27(O27), .in28(O28), .in29(O29), .in30(O30), .in31(O31), .out(Output_2), .sel(in_10));

  // Other names for the same wires on the sheet: Clock = in_4; H[31:0] = in_8; L[31:0] = in_9; LM_D = in_11; R = in_5;
  //   V[31:0] = in_6
endmodule

module ALU (
  input  [31:0] in_1,
  input  [31:0] in_2,
  input  [3:0] in_3,
  output [31:0] Low,
  output Zero_Flag,
  output Negative_Flag,
  output [31:0] High
);

  wire comparator_1_lt, comparator_2_lt;
  wire [31:0] Add, And, Div, DivR, Divu, DivuR, Mul, MulH, Mulu, MuluH, NOr, Or, Slt, Sltu, Sub, XOr;

  Adder #(.width(32)) adder_1 (.a(in_1), .b(in_2), .out(Add));  // open: cin, cout
  Subtractor #(.width(32)) subtractor_1 (.a(in_1), .b(in_2), .out(Sub));  // open: bin, bout
  assign And = in_1 & in_2;  // AND_Gate and_1, 32 bits wide
  Multiplier #(.width(32)) multiplier_1 (.a(in_1), .b(in_2), .out(Mulu), .cout(MuluH));  // open: cin
  Signed_Multiplicator signed_multiplicator_1 (.out_3(Mul), .in_1(in_1), .out_4(MulH), .in_2(in_2));
  assign Or = in_1 | in_2;  // OR_Gate or_1, 32 bits wide
  Divider #(.width(32)) divider_1 (.a(in_1), .b(in_2), .out(Divu), .rem(DivR));  // open: upper
  Signed_Divisor signed_divisor_1 (.out_3(Div), .out_4(DivuR), .in_1(in_1), .in_2(in_2));
  assign NOr = ~(in_1 | in_2);  // NOR_Gate nor_1, 32 bits wide
  Comparator #(.width(32), .mode("unsigned")) comparator_1 (.a(in_1), .b(in_2), .lt(comparator_1_lt));  // open: gt, eq
  assign Sltu = {{31{1'b0}}, comparator_1_lt};  // Bit_Extender bit_extender_1
  Comparator #(.width(32)) comparator_2 (.a(in_1), .b(in_2), .lt(comparator_2_lt));  // open: gt, eq
  assign Slt = {{31{1'b0}}, comparator_2_lt};  // Bit_Extender bit_extender_2
  assign XOr = in_1 ^ in_2;  // XOR_Gate xor_1, 32 bits wide
  // Probe on Low
  Multiplexer #(.select(4), .width(32), .enable("false")) multiplexer_1 (
    .in0(Add), .in1(Sub), .in2(And), .in3(Or), .in4(NOr), .in5(XOr), .in6(Slt), .in7(Sltu), .in8(Mul),
    .in9(Mulu), .in10(Div), .in11(Divu), .in12(in_1), .out(Low), .sel(in_3));  // open: in13, in14, in15
  Multiplexer #(.select(2), .width(32)) multiplexer_2 (
    .in0(MulH), .in1(MuluH), .in2(DivR), .in3(DivuR), .out(High), .sel(in_3[1:0]), .en(in_3[3]));
  Comparator #(.width(32)) comparator_3 (.a(Low), .b({32{1'b0}}), .eq(Zero_Flag), .lt(Negative_Flag));  // open: gt

  // Other names for the same wires on the sheet: A[31:0] = in_1; B[31:0] = in_2; Op[3:0] = in_3;
  //   OpHR[1:0] = in_3[1:0]; En = in_3[3]

  // Notes on the sheet:
  //   in_2: pull=down
  //   in_3: pull=down
  //   in_1: pull=down
endmodule

module Signed_Multiplicator (
  input  [31:0] in_1,
  input  [31:0] in_2,
  output [31:0] out_3,
  output [31:0] out_4
);

  wire adder_1_cout, xor_1_out;
  wire [31:0] adder_1_out, adder_2_out, bit_extender_1_out, multiplexer_1_out, multiplexer_2_out,
       multiplier_1_cout, multiplier_1_out, negator_1_out, negator_2_out, not_1_out, not_2_out;

  Negator #(.width(32)) negator_1 (.in(in_1), .out(negator_1_out));
  Negator #(.width(32)) negator_2 (.in(in_2), .out(negator_2_out));
  Multiplexer #(.width(32), .enable("false")) multiplexer_1 (
    .in0(in_1), .in1(negator_1_out), .out(multiplexer_1_out), .sel(in_1[31]));
  Multiplexer #(.width(32), .enable("false")) multiplexer_2 (
    .in0(in_2), .in1(negator_2_out), .out(multiplexer_2_out), .sel(in_2[31]));
  assign not_1_out = ~multiplier_1_out;  // NOT_Gate not_1, 32 bits wide
  Multiplier #(.width(32)) multiplier_1 (
    .a(multiplexer_1_out), .b(multiplexer_2_out), .out(multiplier_1_out), .cout(multiplier_1_cout));  // open: cin
  xor xor_1 (xor_1_out, in_1[31], in_2[31]);
  Adder #(.width(32)) adder_1 (.a(not_1_out), .b(32'h1), .out(adder_1_out), .cout(adder_1_cout));  // open: cin
  assign not_2_out = ~multiplier_1_cout;  // NOT_Gate not_2, 32 bits wide
  Multiplexer #(.width(32), .enable("false")) multiplexer_3 (
    .in0(multiplier_1_out), .in1(adder_1_out), .out(out_3), .sel(xor_1_out));
  assign bit_extender_1_out = {{31{1'b0}}, adder_1_cout};  // Bit_Extender bit_extender_1
  Multiplexer #(.width(32), .enable("false")) multiplexer_4 (
    .in0(multiplier_1_cout), .in1(adder_2_out), .out(out_4), .sel(xor_1_out));
  Adder #(.width(32)) adder_2 (.a(not_2_out), .b(bit_extender_1_out), .out(adder_2_out));  // open: cin, cout
endmodule

module Signed_Divisor (
  input  [31:0] in_1,
  input  [31:0] in_2,
  output [31:0] out_3,
  output [31:0] out_4
);

  wire xor_1_out;
  wire [31:0] divider_1_out, multiplexer_1_out, multiplexer_2_out, negator_1_out, negator_2_out,
       negator_3_out;

  Negator #(.width(32)) negator_1 (.in(in_1), .out(negator_1_out));
  Negator #(.width(32)) negator_2 (.in(in_2), .out(negator_2_out));
  Multiplexer #(.width(32), .enable("false")) multiplexer_1 (
    .in0(in_1), .in1(negator_1_out), .out(multiplexer_1_out), .sel(in_1[31]));
  Multiplexer #(.width(32), .enable("false")) multiplexer_2 (
    .in0(in_2), .in1(negator_2_out), .out(multiplexer_2_out), .sel(in_2[31]));
  Divider #(.width(32)) divider_1 (
    .a(multiplexer_1_out), .b(multiplexer_2_out), .out(divider_1_out), .rem(out_4));  // open: upper
  xor xor_1 (xor_1_out, in_1[31], in_2[31]);
  Negator #(.width(32)) negator_3 (.in(divider_1_out), .out(negator_3_out));
  Multiplexer #(.width(32), .enable("false")) multiplexer_3 (
    .in0(divider_1_out), .in1(negator_3_out), .out(out_3), .sel(xor_1_out));
endmodule

module Data_Path (
  input  in_1,
  input  in_2,
  input  in_3,
  input  in_4,
  input  in_5,
  input  in_6,
  input  [1:0] in_7,
  input  [1:0] in_8,
  input  [3:0] in_9,
  input  [31:0] in_10,
  input  [31:0] in_11,
  input  [31:0] in_12,
  input  [31:0] in_13,
  input  [31:0] in_14,
  output out_15,
  output out_16,
  output out_17,
  output out_18,
  output out_19,
  output out_20,
  output [1:0] out_21,
  output [1:0] out_22,
  output [2:0] out_23,
  output [3:0] out_24,
  output [15:0] out_25,
  output [31:0] out_26,
  output [31:0] TTY
);

  wire alu_1_negative_flag, alu_1_zero_flag, and_7_out, and_8_out, instruction_decoder_1_out_6,
       instruction_decoder_1_out_8, instruction_decoder_1_out_18, Mul_Div, not_1_out, not_2_out, Push_Pop;
  wire [1:0] and_1_out, Indx_b;
  wire [2:0] instruction_decoder_1_out_19;
  wire [3:0] instruction_decoder_1_operation, Mask, OutMask;
  wire [4:0] instruction_decoder_1_out_5, instruction_decoder_1_out_7, instruction_decoder_1_out_9,
       multiplexer_4_out, multiplexer_6_out;
  wire [15:0] instruction_decoder_1_out_17, RAM_Adr;
  wire [25:0] instruction_decoder_1_out_16;
  wire [31:0] alu_1_high, bit_extender_1_out, bit_extender_2_out, branch_control_unit_1_out_9,
       \instruction_memory_caché_1_out_11 , multiplexer_1_out, multiplexer_5_out, multiplexer_7_out,
       multiplexer_8_out, multiplexer_9_out, O2, Out, PC, random_1_out, register_file_1_output_high___low,
       Value;

  Multiplexer #(.width(32), .enable("false")) multiplexer_1 (
    .in0(Out), .in1(O2), .out({multiplexer_1_out[31:4], out_21, multiplexer_1_out[1:0]}), .sel(Push_Pop));
  Multiplexer #(.select(2), .width(32), .enable("false")) multiplexer_2 (
    .in0(in_10), .in1(in_11), .in2(in_12), .in3(in_13),
    .out({Value[7:0], Value[15:8], Value[23:16], Value[31:24]}), .sel(out_21));
  // Probe on out_21
  not not_1 (not_1_out, out_23[2]);
  not not_2 (not_2_out, out_23[1]);
  and and_1 (and_1_out[0], out_23[1], not_1_out, out_16);
  and and_2 (and_1_out[1], not_2_out, out_23[2], out_16);
  Multiplexer #(.select(2), .width(16), .enable("false")) multiplexer_3 (
    .in0(RAM_Adr), .in1(Out[19:4]), .in2(O2[19:4]), .out(out_25), .sel(and_1_out));  // open: in3
  // Probe on Value
  and and_3 (OutMask[0], ~out_21[0], ~out_21[1]);  // AND_Gate
  and and_4 (OutMask[2], ~out_21[0], out_21[1]);  // AND_Gate
  \Instruction_Memory__Caché  \instruction_memory_caché_1  (
    .in_1(in_10), .in_2(in_11), .in_3(in_12), .in_4(in_13), .Adress_Instruction(PC), .in_6(in_3),
    .in_7(in_1), .in_10(in_9), .out_11(\instruction_memory_caché_1_out_11 ), .out_12(RAM_Adr),
    .out_16(out_16), .RAM_RW(out_18), .Mask(Mask), .CS(out_20), .in_8(in_2), .RAM_Adress(out_25));
  and and_5 (OutMask[1], out_21[0], ~out_21[1]);  // AND_Gate
  and and_6 (OutMask[3], out_21[0], out_21[1]);
  Instruction_Decoder instruction_decoder_1 (
    .in_1(\instruction_memory_caché_1_out_11 ), .out_16(instruction_decoder_1_out_16),
    .out_17(instruction_decoder_1_out_17), .Operation(instruction_decoder_1_operation),
    .out_5(instruction_decoder_1_out_5), .out_6(instruction_decoder_1_out_6),
    .out_7(instruction_decoder_1_out_7), .out_8(instruction_decoder_1_out_8),
    .out_9(instruction_decoder_1_out_9), .out_11(Push_Pop), .out_15(Indx_b), .out_12(out_17),
    .out_14(out_19), .out_3(out_23), .out_18(instruction_decoder_1_out_18),
    .out_19(instruction_decoder_1_out_19), .out_4(out_22), .out_13(out_15), .out_10(Mul_Div));
  Multiplexer #(.select(2), .width(5), .enable("false")) multiplexer_4 (
    .in0(instruction_decoder_1_out_9), .in1(instruction_decoder_1_out_7), .in2({5{1'b1}}),
    .out(multiplexer_4_out), .sel(in_8));  // open: in3
  Random #(.width(32)) random_1 (.clk(in_3), .out(random_1_out));  // open: next, clr
  // Probe on instruction_decoder_1_out_7
  and and_7 (and_7_out, Mul_Div, in_5);
  Multiplexer #(.select(2), .width(32), .enable("false")) multiplexer_5 (
    .in0(Out), .in1(random_1_out), .in2(in_14), .in3(Value), .out(multiplexer_5_out), .sel(in_7));
  Multiplexer #(.width(5), .enable("false")) multiplexer_6 (
    .in0(instruction_decoder_1_out_7), .in1({5{1'b1}}), .out(multiplexer_6_out), .sel(Push_Pop));
  and and_8 (and_8_out, ~Mul_Div, in_5);  // AND_Gate
  Register_File register_file_1 (
    .in_4(in_3), .in_5(in_1), .in_6(multiplexer_5_out), .RW(and_8_out), .Adress(multiplexer_4_out),
    .in_2(instruction_decoder_1_out_5), .in_10(multiplexer_6_out), .Output_1(TTY), .Output_2(O2),
    .in_8(alu_1_high), .in_9(Out), .Output_High___Low(register_file_1_output_high___low),
    .in_7(instruction_decoder_1_out_8), .in_11(and_7_out));
  assign bit_extender_1_out = {{16{1'b0}}, instruction_decoder_1_out_17};  // Bit_Extender bit_extender_1
  assign bit_extender_2_out = {{16{instruction_decoder_1_out_17[15]}}, instruction_decoder_1_out_17};  // Bit_Extender bit_extender_2
  Branch_Control_Unit branch_control_unit_1 (
    .in_5(alu_1_negative_flag), .Branch_Jump(bit_extender_2_out), .in_2(instruction_decoder_1_out_16),
    .in_3(TTY), .in_6(alu_1_zero_flag), .in_7(instruction_decoder_1_out_18),
    .out_9(branch_control_unit_1_out_9), .in_4(PC), .in_8(instruction_decoder_1_out_19));
  Multiplexer #(.width(32), .enable("false")) multiplexer_7 (
    .in0(TTY), .in1(O2), .out(multiplexer_7_out), .sel(Push_Pop));
  // Probe on O2
  Multiplexer #(.select(2), .width(32), .enable("false")) multiplexer_8 (
    .in0(O2), .in1(bit_extender_1_out), .in2(32'h4), .in3(bit_extender_2_out), .out(multiplexer_8_out),
    .sel(Indx_b));
  // Probe on Indx_b
  Register #(.width(32)) register_1 (.D(branch_control_unit_1_out_9), .en(in_6), .Q(PC), .clk(in_3), .clr(in_1));
  Multiplexer #(.width(32), .enable("false")) multiplexer_9 (
    .in0(multiplexer_7_out), .in1(register_file_1_output_high___low), .out(multiplexer_9_out),
    .sel(instruction_decoder_1_out_6));
  // Probe on multiplexer_8_out
  ALU alu_1 (
    .in_1(multiplexer_9_out), .in_2(multiplexer_8_out), .Low(Out), .Zero_Flag(alu_1_zero_flag),
    .Negative_Flag(alu_1_negative_flag), .in_3(instruction_decoder_1_operation), .High(alu_1_high));
  Multiplexer #(.width(4), .enable("false")) multiplexer_10 (.in0(Mask), .in1(OutMask), .out(out_24), .sel(in_4));
  Multiplexer #(.width(32), .enable("false")) multiplexer_11 (.in0(O2), .in1(TTY), .out(out_26), .sel(Push_Pop));

  // Other names for the same wires on the sheet: Sel_Out[1:0] = out_21; SO0 = out_21[0]; SO1 = out_21[1];
  //   Adr[15:0] = out_25; ChipS = out_20; Clock = in_3; Enable_PC = in_6; End = out_16; I0[31:0] = in_10;
  //   I1[31:0] = in_11; I2[31:0] = in_12; I3[31:0] = in_13; I_Type = out_15; Ins_Code[2:0] = out_23;
  //   kbd[31:0] = in_14; L_S = out_19; O1[31:0] = TTY; Pop = out_17; RandW = in_5; RandW_RAM = out_18;
  //   ReadTime[3:0] = in_9; Reset = in_1; RW_C = in_2; RW_R = in_4; Sel_Special[1:0] = out_22; SelAdr[1:0] = in_8;
  //   SelV[1:0] = in_7
endmodule

module Instruction_Decoder (
  input  [31:0] in_1,
  output [3:0] Operation,
  output [2:0] out_3,
  output [1:0] out_4,
  output [4:0] out_5,
  output out_6,
  output [4:0] out_7,
  output out_8,
  output [4:0] out_9,
  output out_10,
  output out_11,
  output out_12,
  output out_13,
  output out_14,
  output [1:0] out_15,
  output [25:0] out_16,
  output [15:0] out_17,
  output out_18,
  output [2:0] out_19
);

  wire Addi, and_9_out, and_27_out, and_28_out, and_29_out, and_30_out, and_31_out, and_32_out, and_33_out,
       and_34_out, and_35_out, and_36_out, and_37_out, and_38_out, and_39_out, and_40_out, and_41_out,
       Branch, halt, I_Type_Inmediate, I_Type_Lw_Sw, J_Type, Jr, kbd, nand_1_out, None, Nop, or_4_out, Push,
       R_M, R_type_A, R_Type_ALU, R_Type_Inst_E, rnd, Slti, Sw, tty, W_M, WR_RF;

  and and_1 (out_11, ~in_1[26], ~in_1[27], ~in_1[28], in_1[29], in_1[30], in_1[31]);  // AND_Gate
  and and_2 (Addi, ~in_1[26], ~in_1[27], ~in_1[28], in_1[29], ~in_1[30], ~in_1[31]);  // AND_Gate
  and and_3 (R_type_A, ~in_1[26], ~in_1[27], ~in_1[28], ~in_1[29], ~in_1[30], ~in_1[31]);  // AND_Gate
  and u_J_Type (J_Type, ~in_1[26], in_1[27], ~in_1[28], ~in_1[29], ~in_1[30], ~in_1[31]);  // AND_Gate
  and and_4 (Nop, ~in_1[0], ~in_1[2], ~in_1[1], R_Type_ALU, ~in_1[3], ~in_1[4], ~in_1[5]);  // AND_Gate
  and and_5 (R_Type_Inst_E, in_1[26], in_1[27], in_1[28], in_1[29], in_1[30], in_1[31]);
  and and_6 (I_Type_Inmediate, out_13, ~in_1[31], ~in_1[30], in_1[29]);  // AND_Gate
  and and_7 (I_Type_Lw_Sw, out_13, in_1[31]);
  and and_8 (out_10, R_Type_ALU, ~in_1[5], in_1[4], in_1[3]);  // AND_Gate
  nand nand_1 (nand_1_out, in_1[28], ~in_1[27]);  // NAND_Gate
  buf and_9 (and_9_out, nand_1_out);  // AND_Gate
  or or_1 (out_15[0], I_Type_Inmediate, I_Type_Lw_Sw);
  or or_2 (None, Nop, out_18);
  and and_10 (halt, R_Type_Inst_E, in_1[2], in_1[1], in_1[0]);
  and and_11 (rnd, R_Type_Inst_E, ~halt, in_1[1]);  // AND_Gate
  and and_12 (kbd, in_1[2], ~in_1[0], ~in_1[1], R_Type_Inst_E);  // AND_Gate
  and and_13 (tty, R_Type_Inst_E, in_1[0], ~in_1[1], ~in_1[2]);  // AND_Gate
  and and_14 (out_14, ~in_1[29], I_Type_Lw_Sw);  // AND_Gate
  and and_15 (Sw, I_Type_Lw_Sw, in_1[29]);
  or or_3 (out_15[1], Slti, out_11, Addi);
  and and_16 (out_12, out_11, ~in_1[0]);  // AND_Gate
  and and_17 (Push, in_1[0], out_11);
  and and_18 (out_13, ~J_Type, ~R_Type_Inst_E, ~R_Type_ALU, ~out_11);  // AND_Gate
  and and_19 (Branch, out_13, ~in_1[29], ~in_1[30], ~in_1[31]);  // AND_Gate
  and and_20 (Jr, ~in_1[0], ~in_1[2], ~in_1[1], in_1[3], ~in_1[4], ~in_1[5], R_type_A);  // AND_Gate
  or or_4 (or_4_out, R_Type_ALU, I_Type_Inmediate);
  or or_5 (W_M, out_14, Push);
  or or_6 (R_M, Sw, out_12);
  or or_7 (out_4[0], tty, kbd);
  or or_8 (out_4[1], kbd, rnd);
  or or_9 (out_18, Branch, Jr, J_Type);
  Multiplexer #(.width(3), .enable("false")) multiplexer_1 (.in0(in_1[28:26]), .in1(in_1[2:0]), .out(out_19), .sel(Jr));
  and and_21 (WR_RF, or_4_out, ~None);  // AND_Gate
  Priority_Encoder priority_encoder_1 (
    .in0(None), .in1(WR_RF), .in2(Sw), .in3(out_14), .in4(Push), .in5(out_12), .in6(R_Type_Inst_E),
    .out(out_3));  // open: in7, en_in, gs, en_out
  and and_22 (Slti, ~in_1[26], in_1[27], ~in_1[28], in_1[29], ~in_1[30], ~in_1[31]);  // AND_Gate
  and and_23 (R_Type_ALU, ~in_1[26], ~in_1[27], ~in_1[28], ~in_1[29], ~in_1[30], ~in_1[31]);  // AND_Gate
  and and_24 (out_6, R_Type_ALU, ~in_1[3], in_1[4], ~in_1[5]);  // AND_Gate
  and and_25 (out_8, out_6, in_1[1]);
  and and_26 (Operation[3], ~in_1[29], ~in_1[28], ~in_1[26], in_1[4], in_1[3]);  // AND_Gate
  and and_27 (and_27_out, ~in_1[29], ~in_1[28], ~in_1[26], in_1[2], in_1[1]);  // AND_Gate
  and and_28 (and_28_out, ~in_1[29], ~in_1[28], ~in_1[26], in_1[5], in_1[3]);  // AND_Gate
  and and_29 (and_29_out, in_1[29], in_1[27], ~in_1[26]);  // AND_Gate
  and and_30 (and_30_out, ~in_1[29], ~in_1[28], ~in_1[26], in_1[2], ~in_1[1]);  // AND_Gate
  and and_31 (and_31_out, ~in_1[29], ~in_1[28], ~in_1[26], in_1[3], in_1[1]);  // AND_Gate
  and and_32 (and_32_out, ~in_1[28], in_1[27], ~in_1[26]);  // AND_Gate
  and and_33 (and_33_out, in_1[29], in_1[28], ~in_1[27]);  // AND_Gate
  or or_10 (Operation[2], and_27_out, and_28_out, and_29_out);
  or or_11 (Operation[1], and_30_out, and_31_out, and_32_out, and_33_out);
  and and_34 (and_34_out, ~in_1[29], in_1[28], ~in_1[27]);  // AND_Gate
  and and_35 (and_35_out, in_1[29], ~in_1[27], in_1[26]);  // AND_Gate
  and and_36 (and_36_out, in_1[29], in_1[28], in_1[27]);
  and and_37 (and_37_out, in_1[30], in_1[0]);
  and and_38 (and_38_out, ~in_1[29], ~in_1[28], ~in_1[26], ~in_1[2], in_1[0]);  // AND_Gate
  and and_39 (and_39_out, ~in_1[29], ~in_1[28], ~in_1[26], ~in_1[1], in_1[0]);  // AND_Gate
  and and_40 (and_40_out, ~in_1[29], ~in_1[28], ~in_1[26], ~in_1[4], ~in_1[3], ~in_1[2], in_1[1]);  // AND_Gate
  and and_41 (and_41_out, ~in_1[29], ~in_1[28], ~in_1[26], in_1[5], in_1[3], ~in_1[1]);  // AND_Gate
  or or_12 (Operation[0], and_38_out, and_39_out, and_40_out, and_41_out, and_34_out, and_35_out, and_36_out, and_37_out);

  assign out_5 = in_1[25:21];
  assign out_7 = in_1[20:16];
  assign out_9 = in_1[15:11];
  assign out_16 = in_1[25:0];
  assign out_17 = in_1[15:0];

  // Other names for the same wires on the sheet: I_Type = out_13; Constant[15:0] = in_1[15:0];
  //   Dest_Jump[25:0] = in_1[25:0]; F_0 = in_1[0]; Func_Code[5:0] = in_1[5:0]; F_1 = in_1[1]; F_2 = in_1[2];
  //   F_3 = in_1[3]; F_4 = in_1[4]; F_5 = in_1[5]; x[4:0] = in_1[10:6]; Rd[4:0] = in_1[15:11]; Rt[4:0] = in_1[20:16];
  //   Rs[4:0] = in_1[25:21]; O_0 = in_1[26]; Op_Code[5:0] = in_1[31:26]; O_1 = in_1[27]; O_2 = in_1[28];
  //   O_3 = in_1[29]; O_4 = in_1[30]; O_5 = in_1[31]; Jmp = out_18; Lw = out_14; Move_from = out_6;
  //   Move_HI_LO = out_8; Mul_Div = out_10; S0 = Operation[0]; S1 = Operation[1]; S2 = Operation[2];
  //   S3 = Operation[3]; Pop = out_12; R_Type_Push_Pop = out_11

  // Notes on the sheet:
  //   in_1: pull=down
  //   Salidas para Register File o ALU
  //   Salidas para el Control Unit
  //   Salidas para el Branch Control Unit
endmodule

module Branch_Control_Unit (
  input  [31:0] Branch_Jump,
  input  [25:0] in_2,
  input  [31:0] in_3,
  input  [31:0] in_4,
  input  in_5,
  input  in_6,
  input  in_7,
  input  [2:0] in_8,
  output [31:0] out_9
);

  wire and_1_out, and_2_out, and_3_out, and_4_out, and_5_out, and_6_out, and_7_out;
  wire [1:0] Jump_Slct;
  wire [31:0] Branch, Next_ins, shifter_1_out;

  Shifter #(.width(32)) shifter_1 (.in(Branch_Jump), .\dist (5'b00010), .out(shifter_1_out));
  Adder #(.width(32)) adder_1 (.a(shifter_1_out), .b(Next_ins), .out(Branch));  // open: cin, cout
  Adder #(.width(32)) adder_2 (.a(in_4), .b(32'h4), .out(Next_ins));  // open: cin, cout
  // Probe on in_3
  and and_1 (and_1_out, ~in_5, in_6, in_7, ~in_8[0], in_8[2]);  // AND_Gate
  and and_2 (and_2_out, ~in_6, in_7, in_8[0], ~in_8[1]);  // AND_Gate
  and and_3 (and_3_out, in_7, ~in_8[2], ~in_8[0], ~in_8[1]);  // AND_Gate
  and and_4 (and_4_out, in_7, ~in_8[2], ~in_8[0], in_8[1]);  // AND_Gate
  and and_5 (and_5_out, ~in_5, ~in_6, in_7, in_8[2], in_8[0]);  // AND_Gate
  and and_6 (and_6_out, in_5, ~in_6, in_7, ~in_8[1], in_8[0]);  // AND_Gate
  and and_7 (and_7_out, in_5, ~in_6, in_7, in_8[1], ~in_8[0]);  // AND_Gate
  or or_1 (Jump_Slct[1], and_3_out, and_4_out);
  or or_2 (Jump_Slct[0], and_4_out, and_5_out, and_1_out, and_2_out, and_6_out, and_7_out);
  Multiplexer #(.select(2), .width(32), .enable("false")) multiplexer_1 (
    .in0(Next_ins), .in1(Branch), .in2(in_3), .in3({in_4[31:28], in_2, 2'b00}), .out(out_9), .sel(Jump_Slct));

  // Other names for the same wires on the sheet: B0 = in_8[0]; B1 = in_8[1]; B2 = in_8[2]; jmp = in_7;
  //   Jump[31:2] = {in_4[31:28], in_2}; Extend[3:0] = in_4[31:28]; Jump_R[31:0] = in_3; N = in_5; Z = in_6

  // Notes on the sheet:
  //   in_5: pull=down
  //   in_8: pull=down
  //   in_7: pull=down
  //   in_6: pull=down
endmodule

module \Instruction_Memory__Caché  (
  input  [31:0] in_1,
  input  [31:0] in_2,
  input  [31:0] in_3,
  input  [31:0] in_4,
  input  [31:0] Adress_Instruction,
  input  in_6,
  input  in_7,
  input  in_8,
  input  [15:0] RAM_Adress,
  input  [3:0] in_10,
  output [31:0] out_11,
  output [15:0] out_12,
  output RAM_RW,
  output [3:0] Mask,
  output CS,
  output out_16
);

  wire comparator_1_eq, comparator_2_eq, d_ff_9_q, EN, EN0, EN1, EN2, EN3, EN4, EN5, EN6, EN7, InCache, Miss,
       nor_1_out, or_1_out, R0, R1, R2, R3, R4, R5, R6, R7, VALIDATE, Value, Value_RAM;
  wire [2:0] multiplexer_1_out;
  wire [3:0] adder_1_out, counter_1_q;
  wire [12:0] Stag, Stag_RAM, Stag_RAM_t, T0, T1, T2, T3, T4, T5, T6, T7;
  wire [31:0] multiplexer_6_out, multiplexer_7_out, multiplexer_8_out, multiplexer_9_out, OP0, OP1, OP2, OP3,
       OP4, OP5, OP6, OP7, OP8, OP9, OP10, OP11, OP12, OP13, OP14, OP15, OP16, OP17, OP18, OP19, OP20, OP21,
       OP22, OP23, OP24, OP25, OP26, OP27, OP28, OP29, OP30, OP31;

  Comparator #(.width(13), .mode("unsigned")) comparator_1 (
    .a(Stag_RAM), .b(RAM_Adress[15:3]), .eq(comparator_1_eq));  // open: gt, lt
  Demultiplexer #(.select(3), .enable("false")) demultiplexer_1 (
    .out0(EN0), .out1(EN1), .out2(EN2), .out3(EN3), .out4(EN4), .out5(EN5), .out6(EN6), .out7(EN7),
    .in(or_1_out), .sel(multiplexer_1_out));
  or or_1 (or_1_out, EN, ~VALIDATE);  // OR_Gate
  Multiplexer #(.width(3), .enable("false")) multiplexer_1 (
    .in0(Adress_Instruction[6:4]), .in1(RAM_Adress[2:0]), .out(multiplexer_1_out), .sel(in_8));
  nand nand_1 (VALIDATE, in_8, InCache);
  and and_1 (InCache, comparator_1_eq, Value_RAM);
  Register #(.width(13)) register_1 (.D(Adress_Instruction[19:7]), .en(EN0), .Q(T0), .clk(in_6), .clr(in_7));
  Register #(.width(13)) register_2 (.D(Adress_Instruction[19:7]), .en(EN1), .Q(T1), .clk(in_6), .clr(in_7));
  Register #(.width(13)) register_3 (.D(Adress_Instruction[19:7]), .en(EN2), .Q(T2), .clk(in_6), .clr(in_7));
  Register #(.width(13)) register_4 (.D(Adress_Instruction[19:7]), .en(EN3), .Q(T3), .clk(in_6), .clr(in_7));
  Register #(.width(13)) register_5 (.D(Adress_Instruction[19:7]), .en(EN4), .Q(T4), .clk(in_6), .clr(in_7));
  Register #(.width(13)) register_6 (.D(Adress_Instruction[19:7]), .en(EN5), .Q(T5), .clk(in_6), .clr(in_7));
  Register #(.width(13)) register_7 (.D(Adress_Instruction[19:7]), .en(EN6), .Q(T6), .clk(in_6), .clr(in_7));
  Register #(.width(13)) register_8 (.D(Adress_Instruction[19:7]), .en(EN7), .Q(T7), .clk(in_6), .clr(in_7));
  Multiplexer #(.select(3), .width(13), .enable("false")) multiplexer_2 (
    .in0(T0), .in1(T1), .in2(T2), .in3(T3), .in4(T4), .in5(T5), .in6(T6), .in7(T7), .out(Stag_RAM_t),
    .sel(RAM_Adress[2:0]));
  Register #(.width(32)) register_9 (.D(in_1), .en(EN0), .Q(OP0), .clk(in_6), .clr(in_7));
  Register #(.width(32)) register_10 (.D(in_1), .en(EN1), .Q(OP4), .clk(in_6), .clr(in_7));
  Register #(.width(32)) register_11 (.D(in_1), .en(EN2), .Q(OP8), .clk(in_6), .clr(in_7));
  Register #(.width(32)) register_12 (.D(in_1), .en(EN3), .Q(OP12), .clk(in_6), .clr(in_7));
  Register #(.width(32)) register_13 (.D(in_1), .en(EN4), .Q(OP16), .clk(in_6), .clr(in_7));
  Register #(.width(32)) register_14 (.D(in_1), .en(EN5), .Q(OP20), .clk(in_6), .clr(in_7));
  Register #(.width(32)) register_15 (.D(in_1), .en(EN6), .Q(OP24), .clk(in_6), .clr(in_7));
  Register #(.width(32)) register_16 (.D(in_1), .en(EN7), .Q(OP28), .clk(in_6), .clr(in_7));
  Register #(.width(32)) register_17 (.D(in_2), .en(EN0), .Q(OP1), .clk(in_6), .clr(in_7));
  Register #(.width(32)) register_18 (.D(in_2), .en(EN1), .Q(OP5), .clk(in_6), .clr(in_7));
  Register #(.width(32)) register_19 (.D(in_2), .en(EN2), .Q(OP9), .clk(in_6), .clr(in_7));
  Register #(.width(32)) register_20 (.D(in_2), .en(EN3), .Q(OP13), .clk(in_6), .clr(in_7));
  Register #(.width(32)) register_21 (.D(in_2), .en(EN4), .Q(OP17), .clk(in_6), .clr(in_7));
  Register #(.width(32)) register_22 (.D(in_2), .en(EN5), .Q(OP21), .clk(in_6), .clr(in_7));
  Register #(.width(32)) register_23 (.D(in_2), .en(EN6), .Q(OP25), .clk(in_6), .clr(in_7));
  Register #(.width(32)) register_24 (.D(in_2), .en(EN7), .Q(OP29), .clk(in_6), .clr(in_7));
  Multiplexer #(.select(3), .enable("false")) multiplexer_3 (
    .in0(R0), .in1(R1), .in2(R2), .in3(R3), .in4(R4), .in5(R5), .in6(R6), .in7(R7), .out(Value_RAM),
    .sel(RAM_Adress[2:0]));
  Register #(.width(32)) register_25 (.D(in_3), .en(EN0), .Q(OP2), .clk(in_6), .clr(in_7));
  Register #(.width(32)) register_26 (.D(in_3), .en(EN1), .Q(OP6), .clk(in_6), .clr(in_7));
  Register #(.width(32)) register_27 (.D(in_3), .en(EN2), .Q(OP10), .clk(in_6), .clr(in_7));
  Register #(.width(32)) register_28 (.D(in_3), .en(EN3), .Q(OP14), .clk(in_6), .clr(in_7));
  Register #(.width(32)) register_29 (.D(in_3), .en(EN4), .Q(OP18), .clk(in_6), .clr(in_7));
  Register #(.width(32)) register_30 (.D(in_3), .en(EN5), .Q(OP22), .clk(in_6), .clr(in_7));
  Register #(.width(32)) register_31 (.D(in_3), .en(EN6), .Q(OP26), .clk(in_6), .clr(in_7));
  Register #(.width(32)) register_32 (.D(in_3), .en(EN7), .Q(OP30), .clk(in_6), .clr(in_7));
  Register #(.width(32)) register_33 (.D(in_4), .en(EN0), .Q(OP3), .clk(in_6), .clr(in_7));
  Register #(.width(32)) register_34 (.D(in_4), .en(EN1), .Q(OP7), .clk(in_6), .clr(in_7));
  Register #(.width(32)) register_35 (.D(in_4), .en(EN2), .Q(OP11), .clk(in_6), .clr(in_7));
  Register #(.width(32)) register_36 (.D(in_4), .en(EN3), .Q(OP15), .clk(in_6), .clr(in_7));
  Register #(.width(32)) register_37 (.D(in_4), .en(EN4), .Q(OP19), .clk(in_6), .clr(in_7));
  Register #(.width(32)) register_38 (.D(in_4), .en(EN5), .Q(OP23), .clk(in_6), .clr(in_7));
  Register #(.width(32)) register_39 (.D(in_4), .en(EN6), .Q(OP27), .clk(in_6), .clr(in_7));
  Register #(.width(32)) register_40 (.D(in_4), .en(EN7), .Q(OP31), .clk(in_6), .clr(in_7));
  not not_1 (Miss, out_16);
  D_Flip_Flop d_ff_1 (.clk(in_6), .D(VALIDATE), .Q(R0), .en(EN0), .reset(in_7));  // open: Qn, preset
  D_Flip_Flop d_ff_2 (.clk(in_6), .D(VALIDATE), .Q(R1), .en(EN1), .reset(in_7));  // open: Qn, preset
  D_Flip_Flop d_ff_3 (.clk(in_6), .D(VALIDATE), .Q(R2), .en(EN2), .reset(in_7));  // open: Qn, preset
  D_Flip_Flop d_ff_4 (.clk(in_6), .D(VALIDATE), .Q(R3), .en(EN3), .reset(in_7));  // open: Qn, preset
  D_Flip_Flop d_ff_5 (.clk(in_6), .D(VALIDATE), .Q(R4), .en(EN4), .reset(in_7));  // open: Qn, preset
  D_Flip_Flop d_ff_6 (.clk(in_6), .D(VALIDATE), .Q(R5), .en(EN5), .reset(in_7));  // open: Qn, preset
  D_Flip_Flop d_ff_7 (.clk(in_6), .D(VALIDATE), .Q(R6), .en(EN6), .reset(in_7));  // open: Qn, preset
  D_Flip_Flop d_ff_8 (.clk(in_6), .D(VALIDATE), .Q(R7), .en(EN7), .reset(in_7));  // open: Qn, preset
  Comparator #(.width(13), .mode("unsigned")) comparator_2 (
    .a(Stag), .b(Adress_Instruction[19:7]), .eq(comparator_2_eq));  // open: gt, lt
  Adder #(.width(4)) adder_1 (.a(in_10), .b(4'b0001), .out(adder_1_out));  // open: cin, cout
  D_Flip_Flop d_ff_9 (.clk(in_6), .D(Miss), .Q(d_ff_9_q));  // open: Qn, preset, en, reset
  and and_2 (out_16, comparator_2_eq, Value);
  Counter #(.width(4), .max('hf)) counter_1 (
    .load(Miss), .D(adder_1_out), .count(d_ff_9_q), .Q(counter_1_q), .clk(in_6));  // open: carry, clr
  nor nor_1 (nor_1_out, counter_1_q[0], counter_1_q[1], counter_1_q[2], counter_1_q[3]);
  Multiplexer #(.select(3), .enable("false")) multiplexer_4 (
    .in0(R0), .in1(R1), .in2(R2), .in3(R3), .in4(R4), .in5(R5), .in6(R6), .in7(R7), .out(Value),
    .sel(Adress_Instruction[6:4]));
  Multiplexer #(.select(3), .width(13), .enable("false")) multiplexer_5 (
    .in0(T0), .in1(T1), .in2(T2), .in3(T3), .in4(T4), .in5(T5), .in6(T6), .in7(T7), .out(Stag),
    .sel(Adress_Instruction[6:4]));
  and and_3 (EN, nor_1_out, d_ff_9_q);
  Multiplexer #(.select(3), .width(32), .enable("false")) multiplexer_6 (
    .in0(OP0), .in1(OP4), .in2(OP8), .in3(OP12), .in4(OP16), .in5(OP20), .in6(OP24), .in7(OP28),
    .out(multiplexer_6_out), .sel(Adress_Instruction[6:4]));
  Multiplexer #(.select(3), .width(32), .enable("false")) multiplexer_7 (
    .in0(OP1), .in1(OP5), .in2(OP9), .in3(OP13), .in4(OP17), .in5(OP21), .in6(OP25), .in7(OP29),
    .out(multiplexer_7_out), .sel(Adress_Instruction[6:4]));
  Multiplexer #(.select(3), .width(32), .enable("false")) multiplexer_8 (
    .in0(OP2), .in1(OP6), .in2(OP10), .in3(OP14), .in4(OP18), .in5(OP22), .in6(OP26), .in7(OP30),
    .out(multiplexer_8_out), .sel(Adress_Instruction[6:4]));
  Multiplexer #(.select(3), .width(32), .enable("false")) multiplexer_9 (
    .in0(OP3), .in1(OP7), .in2(OP11), .in3(OP15), .in4(OP19), .in5(OP23), .in6(OP27), .in7(OP31),
    .out(multiplexer_9_out), .sel(Adress_Instruction[6:4]));
  Multiplexer #(.select(2), .width(32), .enable("false")) multiplexer_10 (
    .in0(multiplexer_6_out), .in1(multiplexer_7_out), .in2(multiplexer_8_out), .in3(multiplexer_9_out),
    .out({out_11[7:0], out_11[15:8], out_11[23:16], out_11[31:24]}), .sel(Adress_Instruction[3:2]));
  // Probe on Adress_Instruction[3:2]
  and and_4 (CS, ~in_7, Miss);  // AND_Gate

  assign Mask = 4'b1111;
  assign out_12 = Adress_Instruction[19:4];
  assign RAM_RW = 1'b0;

  // Other names for the same wires on the sheet: offset[1:0] = Adress_Instruction[3:2];
  //   index[2:0] = Adress_Instruction[6:4]; RAM_adress_t[15:0] = Adress_Instruction[19:4];
  //   tag[12:0] = Adress_Instruction[19:7]; Clk = in_6; Hit = out_16; IP0[31:0] = in_1; IP1[31:0] = in_2;
  //   IP2[31:0] = in_3; IP3[31:0] = in_4; index_RAM[2:0] = RAM_Adress[2:0]; tag_RAM[12:0] = RAM_Adress[15:3];
  //   Rst = in_7; RW = in_8

  // Notes on the sheet:
  //   out_16: pull=down
  //   RAM_Adress: pull=down
endmodule

module Control_Unit (
  input  in_1,
  input  in_2,
  input  in_3,
  input  in_4,
  input  in_5,
  input  in_6,
  input  [1:0] in_7,
  input  [3:0] in_8,
  input  [2:0] Ins_C,
  input  [3:0] in_10,
  output Halt,
  output [1:0] SelAdr,
  output out_13,
  output [1:0] SelV,
  output out_15,
  output out_16,
  output out_17,
  output out_18,
  output out_19,
  output out_20
);

  wire and_1_out, and_3_out, and_4_out, and_6_out, CS0, CS1, CS2, CS3, d_ff_1_q, d_ff_2_q, d_ff_3_q,
       d_ff_4_q, d_ff_9_q, d_ff_13_q, demultiplexer_1_out0, demultiplexer_1_out1, demultiplexer_2_out0,
       demultiplexer_2_out2, demultiplexer_2_out3, demultiplexer_2_out4, demultiplexer_2_out5,
       demultiplexer_2_out6, demultiplexer_3_out0, demultiplexer_4_out0, demultiplexer_5_out0,
       demultiplexer_6_out0, demultiplexer_7_out0, nor_1_out, or_8_out, or_9_out, or_11_out, or_12_out,
       or_13_out, or_14_out, or_15_out, RW_0, RW_1, RW_2, RW_3, RW_4, RW_5, RW_6, RW_C0, RW_C1, \wait ;
  wire [3:0] counter_1_q, RorW;

  Multiplexer #(.width(4), .enable("false")) multiplexer_1 (.in0(in_8), .in1(in_10), .out(RorW), .sel(out_20));
  or or_1 (SelAdr[1], RW_4, RW_2);
  or or_2 (out_13, CS0, CS1, CS2, CS3);
  and and_1 (and_1_out, RW_0, in_4);
  or or_3 (SelV[0], RW_3, RW_5, RW_1);
  or or_4 (SelV[1], RW_3, RW_6, RW_1);
  or or_5 (out_18, RW_0, RW_1, RW_2, RW_3, RW_4, RW_5, RW_6);
  or or_6 (out_20, CS0, CS2);
  or or_7 (SelAdr[0], and_1_out, RW_1);
  or or_8 (or_8_out, in_1, ~in_3);  // OR_Gate
  D_Flip_Flop d_ff_1 (.clk(in_2), .D(demultiplexer_1_out0), .Q(d_ff_1_q), .preset(or_8_out));  // open: Qn, en, reset
  Demultiplexer #(.enable("false")) demultiplexer_1 (
    .out0(demultiplexer_1_out0), .out1(demultiplexer_1_out1), .in(or_9_out), .sel(in_3));
  or or_9 (or_9_out, d_ff_1_q, d_ff_13_q);
  D_Flip_Flop d_ff_2 (.clk(in_2), .D(out_13), .Q(d_ff_2_q), .reset(in_1));  // open: Qn, preset, en
  or or_10 (out_19, RW_C0, RW_C1);
  Counter #(.width(4), .max('hf)) counter_1 (
    .load(out_13), .D(RorW), .count(d_ff_2_q), .Q(counter_1_q), .clk(in_2));  // open: carry, clr
  D_Flip_Flop d_ff_3 (.clk(in_2), .D(demultiplexer_1_out1), .Q(d_ff_3_q), .reset(in_1));  // open: Qn, preset, en
  Demultiplexer #(.select(3), .enable("false")) demultiplexer_2 (
    .out0(demultiplexer_2_out0), .out1(RW_0), .out2(demultiplexer_2_out2), .out3(demultiplexer_2_out3),
    .out4(demultiplexer_2_out4), .out5(demultiplexer_2_out5), .out6(demultiplexer_2_out6), .in(d_ff_3_q),
    .sel(Ins_C));  // open: out7
  nor nor_1 (nor_1_out, counter_1_q[0], counter_1_q[1], counter_1_q[2], counter_1_q[3]);
  and and_2 (\wait , nor_1_out, d_ff_2_q);
  and and_3 (and_3_out, demultiplexer_2_out2, ~in_6);  // AND_Gate
  and and_4 (and_4_out, demultiplexer_2_out3, in_6);
  and and_5 (RW_2, demultiplexer_2_out4, ~in_5);  // AND_Gate
  and and_6 (and_6_out, demultiplexer_2_out5, in_5);
  D_Flip_Flop d_ff_4 (.clk(in_2), .D(RW_2), .Q(d_ff_4_q), .reset(in_1));  // open: Qn, preset, en
  Demultiplexer #(.select(2), .enable("false")) demultiplexer_3 (
    .out0(demultiplexer_3_out0), .out1(out_15), .out2(RW_5), .out3(RW_6), .in(demultiplexer_2_out6),
    .sel(in_7));
  or or_11 (or_11_out, demultiplexer_4_out0, and_3_out);
  or or_12 (or_12_out, demultiplexer_5_out0, and_4_out);
  or or_13 (or_13_out, demultiplexer_6_out0, d_ff_4_q);
  or or_14 (or_14_out, demultiplexer_7_out0, and_6_out);
  D_Flip_Flop d_ff_5 (.clk(in_2), .D(or_11_out), .Q(CS0), .reset(in_1));  // open: Qn, preset, en
  D_Flip_Flop d_ff_6 (.clk(in_2), .D(or_12_out), .Q(CS1), .reset(in_1));  // open: Qn, preset, en
  D_Flip_Flop d_ff_7 (.clk(in_2), .D(or_13_out), .Q(CS2), .reset(in_1));  // open: Qn, preset, en
  D_Flip_Flop d_ff_8 (.clk(in_2), .D(or_14_out), .Q(CS3), .reset(in_1));  // open: Qn, preset, en
  D_Flip_Flop d_ff_9 (.clk(in_2), .D(out_15), .Q(d_ff_9_q), .reset(in_1));  // open: Qn, preset, en
  Demultiplexer #(.enable("false")) demultiplexer_4 (.out0(demultiplexer_4_out0), .out1(RW_C0), .in(CS0), .sel(\wait ));
  Demultiplexer #(.enable("false")) demultiplexer_5 (.out0(demultiplexer_5_out0), .out1(RW_1), .in(CS1), .sel(\wait ));
  Demultiplexer #(.enable("false")) demultiplexer_6 (.out0(demultiplexer_6_out0), .out1(RW_C1), .in(CS2), .sel(\wait ));
  Demultiplexer #(.enable("false")) demultiplexer_7 (.out0(demultiplexer_7_out0), .out1(RW_3), .in(CS3), .sel(\wait ));
  D_Flip_Flop d_ff_10 (.clk(in_2), .D(RW_6), .Q(out_16), .reset(in_1));  // open: Qn, preset, en
  or or_15 (or_15_out, d_ff_9_q, RW_5, out_16);
  D_Flip_Flop d_ff_11 (.clk(in_2), .D(RW_3), .Q(RW_4), .reset(in_1));  // open: Qn, preset, en
  D_Flip_Flop d_ff_12 (
    .clk(in_2), .D(demultiplexer_3_out0), .Q(Halt), .en(demultiplexer_3_out0), .reset(in_1));  // open: Qn, preset
  or or_16 (out_17, demultiplexer_2_out0, RW_0, RW_C0, RW_1, RW_C1, RW_4, or_15_out);
  D_Flip_Flop d_ff_13 (.clk(in_2), .D(out_17), .Q(d_ff_13_q), .reset(in_1));  // open: Qn, preset, en

  // Other names for the same wires on the sheet: Clock = in_2; CS = out_13; E__Kbd = out_16; E_PC = out_17;
  //   I___Type = in_4; L_S = in_6; LTTY = out_15; Push_Pop = in_5; Reset = in_1; RorW_0 = CS0; RorW_1 = CS2;
  //   RW_RAM = out_20; SelAdr_00_or_01 = RW_0; SelAdr_10 = RW_4; SelAdr_10_prime = RW_2; SelV_01 = RW_5;
  //   SelV_10 = RW_6; SelV_11 = RW_3; SelAdr_01 = RW_1; SelV_11_prime = RW_1; Special[1:0] = in_7; Start = in_3
endmodule
